// Logisim project Guia_08.circ as structural Verilog: 10 circuits, main circuit Guia_0801_AU_Somador4bits
module main (
);


  // Notes on the sheet:
  //   Guia 08 - Logisim
  //   Matricula: 897891   Nome: Lucas Junio Quirino Teixeira
endmodule

// HA
module halfAdder (
  input  a,
  input  b,
  output s0,
  output s1
);

  // XOR_Gate xor_1 has open pins: out=s0
  and and_1 (s1, a, a);

  assign b = a;

  // Notes on the sheet:
  //   Guia_08 - meia-soma (modelo compacto)
endmodule

// FA
module fullAdder (
  input  a,
  input  b,
  input  carryIn,
  output s0,
  output s1_carryOut
);

  wire and_1_out, and_2_out;

  // XOR_Gate xor_1 has open pins: out=carryIn
  and and_1 (and_1_out, a, a);
  // XOR_Gate xor_2 has open pins: out=s0
  and and_2 (and_2_out, carryIn, carryIn);
  or or_1 (s1_carryOut, and_1_out, and_2_out);

  assign b = a;

  // Notes on the sheet:
  //   Guia_08 - somador completo (2 meias-somas + OR)
endmodule

// HD
module halfDiferenca (
  input  x,
  input  y,
  output d,
  output v
);

  not not_1 (x, x);
  // XOR_Gate xor_1 has open pins: out=d
  and and_1 (v, x, x);

  assign y = x;

  // Notes on the sheet:
  //   Guia_08 - meia-diferenca (modelo compacto)
endmodule

// FS
module fullSubtractor (
  input  x,
  input  y,
  input  vemUm,
  output d,
  output vemUm_saida
);

  wire and_1_out, and_2_out, not_2_out, xor_1_out;

  not not_1 (x, x);
  // XOR_Gate xor_1 has open pins: out=xor_1_out
  and and_1 (and_1_out, x, x);
  not not_2 (not_2_out, xor_1_out);
  // XOR_Gate xor_2 has open pins: out=d
  and and_2 (and_2_out, not_2_out, vemUm);
  or or_1 (vemUm_saida, and_1_out, and_2_out);

  assign y = x;

  // Notes on the sheet:
  //   Guia_08 - diferenca completa (2 meias-diferencas + OR)
endmodule

// 01
module Guia_0801_AU_Somador4bits (
  input  carryIn_inicial,
  input  a0,
  input  b0,
  input  a1,
  input  b1,
  input  a2,
  input  b2,
  input  a3,
  input  b3,
  output s4_carryOut,
  output s0,
  output s1,
  output s2,
  output s3
);

  wire and_1_out, and_2_out, and_3_out, and_4_out, and_5_out, and_6_out, and_7_out, and_8_out;

  // XOR_Gate xor_1 has open pins: out=carryIn_inicial
  and and_1 (and_1_out, a0, a0);
  // XOR_Gate xor_2 has open pins: out=carryIn_inicial
  and and_2 (and_2_out, a1, a1);
  // XOR_Gate xor_3 has open pins: out=carryIn_inicial
  and and_3 (and_3_out, a2, a2);
  // XOR_Gate xor_4 has open pins: out=carryIn_inicial
  and and_4 (and_4_out, a3, a3);
  // XOR_Gate xor_5 has open pins: out=s0
  and and_5 (and_5_out, carryIn_inicial, carryIn_inicial);
  // XOR_Gate xor_6 has open pins: out=s1
  and and_6 (and_6_out, carryIn_inicial, carryIn_inicial);
  // XOR_Gate xor_7 has open pins: out=s2
  and and_7 (and_7_out, carryIn_inicial, carryIn_inicial);
  // XOR_Gate xor_8 has open pins: out=s3
  and and_8 (and_8_out, carryIn_inicial, carryIn_inicial);
  or or_1 (carryIn_inicial, and_1_out, and_5_out);
  or or_2 (carryIn_inicial, and_2_out, and_6_out);
  or or_3 (carryIn_inicial, and_3_out, and_7_out);
  or or_4 (s4_carryOut, and_4_out, and_8_out);

  assign b0 = a0;
  assign b1 = a1;
  assign b2 = a2;
  assign b3 = a3;

  // Notes on the sheet:
  //   Guia_0801 - AU somador completo, 4 bits (amplitude), portas nativas
endmodule

// 02
module Guia_0802_AU_Subtrator4bits (
  input  vemUm_inicial,
  input  a0,
  input  b0,
  input  a1,
  input  b1,
  input  a2,
  input  b2,
  input  a3,
  input  b3,
  output vemUm_saida,
  output s0,
  output s1,
  output s2,
  output s3
);

  wire and_1_out, and_2_out, and_3_out, and_4_out, and_5_out, and_6_out, and_7_out, and_8_out;

  not not_1 (a0, a0);
  not not_2 (a1, a1);
  not not_3 (a2, a2);
  not not_4 (a3, a3);
  // XOR_Gate xor_1 has open pins: out=vemUm_inicial
  and and_1 (and_1_out, a0, a0);
  // XOR_Gate xor_2 has open pins: out=vemUm_inicial
  and and_2 (and_2_out, a1, a1);
  // XOR_Gate xor_3 has open pins: out=vemUm_inicial
  and and_3 (and_3_out, a2, a2);
  // XOR_Gate xor_4 has open pins: out=vemUm_inicial
  and and_4 (and_4_out, a3, a3);
  not not_5 (vemUm_inicial, vemUm_inicial);
  not not_6 (vemUm_inicial, vemUm_inicial);
  not not_7 (vemUm_inicial, vemUm_inicial);
  not not_8 (vemUm_inicial, vemUm_inicial);
  // XOR_Gate xor_5 has open pins: out=s0
  and and_5 (and_5_out, vemUm_inicial, vemUm_inicial);
  // XOR_Gate xor_6 has open pins: out=s1
  and and_6 (and_6_out, vemUm_inicial, vemUm_inicial);
  // XOR_Gate xor_7 has open pins: out=s2
  and and_7 (and_7_out, vemUm_inicial, vemUm_inicial);
  // XOR_Gate xor_8 has open pins: out=s3
  and and_8 (and_8_out, vemUm_inicial, vemUm_inicial);
  or or_1 (vemUm_inicial, and_1_out, and_5_out);
  or or_2 (vemUm_inicial, and_2_out, and_6_out);
  or or_3 (vemUm_inicial, and_3_out, and_7_out);
  or or_4 (vemUm_saida, and_4_out, and_8_out);

  assign b0 = a0;
  assign b1 = a1;
  assign b2 = a2;
  assign b3 = a3;

  // Notes on the sheet:
  //   Guia_0802 - AU subtrator completo, 4 bits (amplitude), portas nativas
endmodule

// 03
module Guia_0803_LU_Igual4bits (
  input  a0,
  input  b0,
  input  a1,
  input  b1,
  input  a2,
  input  b2,
  input  a3,
  input  b3,
  output igual
);

  wire and_1_out, and_2_out, not_1_out, not_2_out, not_3_out, not_4_out, xor_1_out, xor_2_out, xor_3_out,
       xor_4_out;

  // XOR_Gate xor_1 has open pins: out=xor_1_out
  // XOR_Gate xor_2 has open pins: out=xor_2_out
  // XOR_Gate xor_3 has open pins: out=xor_3_out
  // XOR_Gate xor_4 has open pins: out=xor_4_out
  not not_1 (not_1_out, xor_1_out);
  not not_2 (not_2_out, xor_2_out);
  not not_3 (not_3_out, xor_3_out);
  not not_4 (not_4_out, xor_4_out);
  and and_1 (and_1_out, not_1_out, not_2_out);
  and and_2 (and_2_out, and_1_out, not_3_out);
  and and_3 (igual, and_2_out, not_4_out);

  // Notes on the sheet:
  //   Guia_0803 - LU comparador de igualdade, 4 bits, portas nativas (XNOR + AND)
endmodule

// 04
module Guia_0804_LU_Desigual4bits (
  input  a0,
  input  b0,
  input  a1,
  input  b1,
  input  a2,
  input  b2,
  input  a3,
  input  b3,
  output desigual
);

  wire or_1_out, or_2_out, xor_1_out, xor_2_out, xor_3_out, xor_4_out;

  // XOR_Gate xor_1 has open pins: out=xor_1_out
  // XOR_Gate xor_2 has open pins: out=xor_2_out
  // XOR_Gate xor_3 has open pins: out=xor_3_out
  // XOR_Gate xor_4 has open pins: out=xor_4_out
  or or_1 (or_1_out, xor_1_out, xor_2_out);
  or or_2 (or_2_out, or_1_out, xor_3_out);
  or or_3 (desigual, or_2_out, xor_4_out);

  // Notes on the sheet:
  //   Guia_0804 - LU comparador de desigualdade, 4 bits, portas nativas (XOR + OR)
endmodule

// 05
module Guia_0805_LU_Complemento2_5bits (
  input  a0,
  input  a1,
  input  a2,
  input  a3,
  input  a4,
  output carry_final_naoUsado,
  output r0,
  output r1,
  output r2,
  output r3,
  output r4
);

  wire and_1_out, and_2_out, and_3_out, and_4_out, and_5_out, and_6_out, and_7_out, and_8_out, and_9_out,
       and_10_out, not_1_out, not_2_out, not_3_out, not_4_out, not_5_out, xor_1_out;

  not not_1 (not_1_out, a0);
  not not_2 (not_2_out, a1);
  not not_3 (not_3_out, a2);
  not not_4 (not_4_out, a3);
  not not_5 (not_5_out, a4);
  // XOR_Gate xor_1 has open pins: out=xor_1_out
  and and_1 (and_1_out, not_1_out, not_1_out);
  // XOR_Gate xor_2 has open pins: out=xor_1_out
  and and_2 (and_2_out, not_2_out, not_2_out);
  // XOR_Gate xor_3 has open pins: out=xor_1_out
  and and_3 (and_3_out, not_3_out, not_3_out);
  // XOR_Gate xor_4 has open pins: out=xor_1_out
  and and_4 (and_4_out, not_4_out, not_4_out);
  // XOR_Gate xor_5 has open pins: out=xor_1_out
  and and_5 (and_5_out, not_5_out, not_5_out);
  // XOR_Gate xor_6 has open pins: out=r0
  and and_6 (and_6_out, xor_1_out, xor_1_out);
  // XOR_Gate xor_7 has open pins: out=r1
  and and_7 (and_7_out, xor_1_out, xor_1_out);
  // XOR_Gate xor_8 has open pins: out=r2
  and and_8 (and_8_out, xor_1_out, xor_1_out);
  // XOR_Gate xor_9 has open pins: out=r3
  and and_9 (and_9_out, xor_1_out, xor_1_out);
  // XOR_Gate xor_10 has open pins: out=r4
  and and_10 (and_10_out, xor_1_out, xor_1_out);
  or or_1 (xor_1_out, and_1_out, and_6_out);
  or or_2 (xor_1_out, and_2_out, and_7_out);
  or or_3 (xor_1_out, and_3_out, and_8_out);
  or or_4 (xor_1_out, and_4_out, and_9_out);
  or or_5 (carry_final_naoUsado, and_5_out, and_10_out);
  // also tied to GND on the sheet: {not_1_out, not_2_out, not_3_out, not_4_out, not_5_out}
  // also tied to VCC on the sheet: xor_1_out

  // Notes on the sheet:
  //   Guia_0805 - LU complemento de 2, 5 bits (complemento de 1 + somador +1)
endmodule
