// Logisim project Guia_05.circ as structural Verilog: 7 circuits, main circuit main
module main (
);


  // Notes on the sheet:
  //   Guia 05 - Logisim
  //   Matricula: 897891   Nome: Lucas Junio Quirino Teixeira
  //   Selecione na lista: Guia_0501, Guia_0502, Guia_0503, Guia_0504, Guia_0505 ou Guia_0506.
  //   Cada circuito usa somente NAND ou somente NOR conforme solicitado no Guia 05.
endmodule

module Guia_0501 (
  input  a,
  input  b,
  output s
);

  wire n2, na;

  // NAND_Gate nand_1: pin names not known; wires that end beside it: a, a, na
  // NAND_Gate nand_2: pin names not known; wires that end beside it: na, b, n2
  // NAND_Gate nand_3: pin names not known; wires that end beside it: n2, n2, s

  // Notes on the sheet:
  //   Guia_0501 - (~a & b) usando somente NAND
  //   s = (~a & b)
  //   NAND1 inverte a; NAND2 forma a saida negada; NAND3 inverte novamente.
endmodule

module Guia_0502 (
  input  a,
  input  b,
  output s
);

  wire n2, nb;

  // NOR_Gate nor_1: pin names not known; wires that end beside it: b, b, nb
  // NOR_Gate nor_2: pin names not known; wires that end beside it: a, nb, n2
  // NOR_Gate nor_3: pin names not known; wires that end beside it: n2, n2, s

  // Notes on the sheet:
  //   Guia_0502 - (a | ~b) usando somente NOR
  //   s = (a | ~b)
  //   NOR1 inverte b; NOR2 forma a saida negada; NOR3 inverte novamente.
endmodule

module Guia_0503 (
  input  a,
  input  b,
  output s
);

  wire n2, na;

  // NAND_Gate nand_1: pin names not known; wires that end beside it: a, a, na
  // NAND_Gate nand_2: pin names not known; wires that end beside it: na, b, n2
  // NAND_Gate nand_3: pin names not known; wires that end beside it: n2, n2, s

  // Notes on the sheet:
  //   Guia_0503 - ~(a | ~b) usando somente NAND
  //   s = ~(a | ~b) = (~a & b)
  //   Equivalencia por De Morgan; implementacao exclusivamente com NAND.
endmodule

module Guia_0504 (
  input  a,
  input  b,
  output s
);

  wire n2, nb;

  // NOR_Gate nor_1: pin names not known; wires that end beside it: b, b, nb
  // NOR_Gate nor_2: pin names not known; wires that end beside it: a, nb, n2
  // NOR_Gate nor_3: pin names not known; wires that end beside it: n2, n2, s

  // Notes on the sheet:
  //   Guia_0504 - ~(~a & b) usando somente NOR
  //   s = ~(~a & b) = (a | ~b)
  //   Equivalencia por De Morgan; implementacao exclusivamente com NOR.
endmodule

module Guia_0505 (
  input  a,
  input  b,
  output s
);

  wire n1, n2, n3;

  // NAND_Gate nand_1: pin names not known; wires that end beside it: a, b, n1
  // NAND_Gate nand_2: pin names not known; wires that end beside it: a, n1, n2
  // NAND_Gate nand_3: pin names not known; wires that end beside it: b, n1, n3
  // NAND_Gate nand_4: pin names not known; wires that end beside it: n2, n3, s

  // Notes on the sheet:
  //   Guia_0505 - XOR usando somente NAND
  //   s = (a ^ b)
  //   XOR implementado com quatro portas NAND.
endmodule

module Guia_0506 (
  input  a,
  input  b,
  output s
);

  wire n1, n2, n3;

  // NOR_Gate nor_1: pin names not known; wires that end beside it: a, b, n1
  // NOR_Gate nor_2: pin names not known; wires that end beside it: a, n1, n2
  // NOR_Gate nor_3: pin names not known; wires that end beside it: b, n1, n3
  // NOR_Gate nor_4: pin names not known; wires that end beside it: n2, n3, s

  // Notes on the sheet:
  //   Guia_0506 - XNOR usando somente NOR
  //   s = ~(a ^ b)
  //   XNOR implementado com quatro portas NOR.
endmodule
