// Logisim project Guia_07.circ as structural Verilog: 6 circuits, main circuit main
module main (
);


  // Notes on the sheet:
  //   Guia 07 - Unidade Logica em Logisim
  //   Matricula: 897891   Nome: Lucas Junio Quirino Teixeira
  //   Abra Guia_0701 a Guia_0705 no painel esquerdo.
  //   Circuitos montados com portas nativas e selecao por MUX 2x1 feito com NOT/AND/OR.
endmodule

module Guia_0701 (
  input  a,
  input  b,
  input  select,
  output and_s,
  output nand_s,
  output s
);

  wire m1_a0, m1_a1, m1_nsel;

  and and_1 (and_s, a, b);
  nand nand_1 (nand_s, a, b);
  not not_1 (m1_nsel, select);
  and and_2 (m1_a0, nand_s, m1_nsel);
  and and_3 (m1_a1, and_s, select);
  or or_1 (s, m1_a0, m1_a1);

  // Notes on the sheet:
  //   Guia_0701 - AND / NAND com saida selecionavel
  //   select=0 -> NAND     select=1 -> AND
  //   MUX 2x1 (s): 0=nand_s  1=and_s
endmodule

module Guia_0702 (
  input  a,
  input  b,
  input  select,
  output s
);

  wire m1_a0, m1_a1, m1_nsel, nor_s, or_s;

  or or_1 (or_s, a, b);
  nor nor_1 (nor_s, a, b);
  not not_1 (m1_nsel, select);
  and and_1 (m1_a0, nor_s, m1_nsel);
  and and_2 (m1_a1, or_s, select);
  or or_2 (s, m1_a0, m1_a1);

  // Notes on the sheet:
  //   Guia_0702 - OR / NOR com saida selecionavel
  //   select=0 -> NOR     select=1 -> OR
  //   MUX 2x1 (s): 0=nor_s  1=or_s
endmodule

module Guia_0703 (
  input  a,
  input  b,
  input  porta,
  input  grupo,
  output s
);

  wire and_s, grupo_and, grupo_or, ma_a0, ma_a1, ma_nsel, mg_a0, mg_a1, mg_nsel, mo_a0, mo_a1, mo_nsel,
       nand_s, nor_s, or_s;

  and and_1 (and_s, a, b);
  nand nand_1 (nand_s, a, b);
  or or_1 (or_s, a, b);
  nor nor_1 (nor_s, a, b);
  not not_1 (ma_nsel, porta);
  not not_2 (mo_nsel, porta);
  and and_2 (ma_a0, nand_s, ma_nsel);
  and and_3 (ma_a1, and_s, porta);
  and and_4 (mo_a0, nor_s, mo_nsel);
  and and_5 (mo_a1, or_s, porta);
  or or_2 (grupo_and, ma_a0, ma_a1);
  or or_3 (grupo_or, mo_a0, mo_a1);
  not not_3 (mg_nsel, grupo);
  and and_6 (mg_a0, grupo_or, mg_nsel);
  and and_7 (mg_a1, grupo_and, grupo);
  or or_4 (s, mg_a0, mg_a1);

  // Notes on the sheet:
  //   Guia_0703 - AND/NAND e OR/NOR com duas selecoes
  //   porta: 0=NAND/NOR, 1=AND/OR   |   grupo: 0=OR/NOR, 1=AND/NAND
  //   MUX 2x1 (grupo_and): 0=nand_s  1=and_s
  //   MUX 2x1 (grupo_or): 0=nor_s  1=or_s
  //   MUX 2x1 (s): 0=grupo_or  1=grupo_and
endmodule

module Guia_0704 (
  input  a,
  input  b,
  input  s0,
  input  s1,
  output s
);

  wire alto, baixo, m0_a0, m0_a1, m0_nsel, m1_a0, m1_a1, m1_nsel, m2_a0, m2_a1, m2_nsel, nor_s, or_s, xnor_s,
       xor_s;

  or or_1 (or_s, a, b);
  nor nor_1 (nor_s, a, b);
  xnor xnor_1 (xnor_s, a, b);
  xor xor_1 (xor_s, a, b);
  not not_1 (m0_nsel, s0);
  not not_2 (m1_nsel, s0);
  and and_1 (m0_a0, or_s, m0_nsel);
  and and_2 (m0_a1, nor_s, s0);
  and and_3 (m1_a0, xnor_s, m1_nsel);
  and and_4 (m1_a1, xor_s, s0);
  or or_2 (baixo, m0_a0, m0_a1);
  or or_3 (alto, m1_a0, m1_a1);
  not not_3 (m2_nsel, s1);
  and and_5 (m2_a0, baixo, m2_nsel);
  and and_6 (m2_a1, alto, s1);
  or or_4 (s, m2_a0, m2_a1);

  // Notes on the sheet:
  //   Guia_0704 - OR / NOR / XOR / XNOR
  //   s1s0: 00=OR, 01=NOR, 10=XNOR, 11=XOR
  //   MUX 2x1 (baixo): 0=or_s  1=nor_s
  //   MUX 2x1 (alto): 0=xnor_s  1=xor_s
  //   MUX 2x1 (s): 0=baixo  1=alto
endmodule

module Guia_0705 (
  input  a,
  input  b,
  input  s0,
  input  s1,
  input  s2,
  output s
);

  wire m01, m01_a0, m01_a1, m01_nsel, m03, m03_a0, m03_a1, m03_nsel, m23, m23_a0, m23_a1, m23_nsel, m45,
       m45_a0, m45_a1, m45_nsel, m47, m47_a0, m47_a1, m47_nsel, m67, m67_a0, m67_a1, m67_nsel, mf_a0, mf_a1,
       mf_nsel, op0, op1, op2, op3, op4, op5, op6, op7;

  not not_1 (op0, a);
  and and_1 (op1, a, b);
  nand nand_1 (op2, a, b);
  or or_1 (op3, a, b);
  nor nor_1 (op4, a, b);
  xor xor_1 (op5, a, b);
  xnor xnor_1 (op6, a, b);
  not not_2 (op7, b);
  not not_3 (m01_nsel, s0);
  not not_4 (m23_nsel, s0);
  not not_5 (m45_nsel, s0);
  not not_6 (m67_nsel, s0);
  and and_2 (m01_a0, op0, m01_nsel);
  and and_3 (m01_a1, op1, s0);
  and and_4 (m23_a0, op2, m23_nsel);
  and and_5 (m23_a1, op3, s0);
  and and_6 (m45_a0, op4, m45_nsel);
  and and_7 (m45_a1, op5, s0);
  and and_8 (m67_a0, op6, m67_nsel);
  and and_9 (m67_a1, op7, s0);
  or or_2 (m01, m01_a0, m01_a1);
  or or_3 (m23, m23_a0, m23_a1);
  or or_4 (m45, m45_a0, m45_a1);
  or or_5 (m67, m67_a0, m67_a1);
  not not_7 (m03_nsel, s1);
  not not_8 (m47_nsel, s1);
  and and_10 (m03_a0, m01, m03_nsel);
  and and_11 (m03_a1, m23, s1);
  and and_12 (m47_a0, m45, m47_nsel);
  and and_13 (m47_a1, m67, s1);
  or or_6 (m03, m03_a0, m03_a1);
  or or_7 (m47, m47_a0, m47_a1);
  not not_9 (mf_nsel, s2);
  and and_14 (mf_a0, m03, mf_nsel);
  and and_15 (mf_a1, m47, s2);
  or or_8 (s, mf_a0, mf_a1);

  // Notes on the sheet:
  //   Guia_0705 - Unidade Logica 8x1
  //   000=NOT a  001=AND  010=NAND  011=OR  100=NOR  101=XOR  110=XNOR  111=NOT b
  //   MUX 2x1 (m01): 0=op0  1=op1
  //   MUX 2x1 (m23): 0=op2  1=op3
  //   MUX 2x1 (m45): 0=op4  1=op5
  //   MUX 2x1 (m67): 0=op6  1=op7
  //   MUX 2x1 (m03): 0=m01  1=m23
  //   MUX 2x1 (m47): 0=m45  1=m67
  //   MUX 2x1 (s): 0=m03  1=m47
endmodule
