// Logisim project Guia_04.circ as structural Verilog: 5 circuits, main circuit main
module main (
);


  // Notes on the sheet:
  //   Guia 04 - Logisim
  //   Matricula: 897891   Nome: Lucas Junio Quirino Teixeira
  //   Selecione na lista de circuitos: Guia_0401, Guia_0402, Guia_0403 ou Guia_0404.
  //   Cada circuito contem os itens a, b, c, d e e da respectiva atividade.
endmodule

module Guia_0401 (
  input  x,
  input  y,
  input  z,
  output a,
  output b,
  output c,
  output d,
  output e
);

  wire n1, n2, n3, n4, n5, n6, n7, n8, n9, n10, n11, nx, ny, nz;

  not not_1 (nx, x);
  not not_2 (ny, y);
  not not_3 (nz, z);
  or or_1 (n1, y, nz);
  or or_2 (n3, x, ny);
  and and_1 (n5, nx, y);
  and and_2 (n7, nx, y);
  or or_3 (n9, nx, ny);
  or or_4 (n10, y, nz);
  not not_4 (n2, n1);
  not not_5 (n4, n3);
  not not_6 (n6, n5);
  not not_7 (n8, n7);
  not not_8 (n11, n10);
  and and_3 (a, x, n2);
  and and_4 (b, n4, z);
  and and_5 (c, n6, nz);
  and and_6 (d, n8, z);
  and and_7 (e, n9, n11);

  // Other names for the same wires on the sheet: s1a = a; s1b = b; s1c = c; s1d = d; s1e = e

  // Notes on the sheet:
  //   Guia_0401 - Tabelas-verdade das proposicoes
  //   a) x . ( y + z' )'
  //   b) ( x + y' )' . z
  //   c) ( x' . y )' . z'
  //   d) ( x' . y )' . z
  //   e) ( x' + y' ) . ( y + z' )'
endmodule

module Guia_0402 (
  input  x,
  input  y,
  input  z,
  output a_orig,
  output a_simp,
  output b_orig,
  output b_simp,
  output c_orig,
  output c_simp,
  output d_orig,
  output d_simp,
  output e_orig,
  output e_simp
);

  wire n1, n2, n3, n4, n5, n6, n7, n8, n9, n10, n11, n12, n13, n14, n15, n16, n17, nx, nz;

  or or_1 (n12, y, nx);
  or or_2 (n14, c_simp, x);
  not not_1 (nx, x);
  not not_2 (c_simp, y);
  not not_3 (nz, z);
  or or_3 (n1, nx, y);
  or or_4 (n3, nx, c_simp);
  and and_1 (n4, x, y);
  and and_2 (n5, x, y);
  or or_5 (n7, x, c_simp);
  and and_3 (n8, nx, y);
  or or_6 (n10, x, c_simp);
  or or_7 (n13, n12, nz);
  or or_8 (n15, n14, z);
  not not_4 (n2, n1);
  not not_5 (n6, n5);
  not not_6 (n9, n8);
  not not_7 (n11, n10);
  or or_9 (b_orig, n3, n4);
  not not_8 (n16, n15);
  and and_4 (n17, y, nx);
  and and_5 (a_orig, x, n2);
  and and_6 (a_simp, x, c_simp);
  or or_10 (b_simp, x, nx);
  and and_7 (c_orig, n6, n7);
  or or_11 (d_orig, n9, n11);
  or or_12 (d_simp, x, nx);
  and and_8 (e_simp, n17, nz);
  and and_9 (e_orig, n13, n16);

  // Other names for the same wires on the sheet: ny = c_simp; o2a = a_orig; o2b = b_orig; o2c = c_orig; o2d = d_orig;
  //   o2e = e_orig; s2a = a_simp; s2b = b_simp; s2d = d_simp; s2e = e_simp

  // Notes on the sheet:
  //   Guia_0402 - Expressoes originais e simplificadas
  //   a) x . ( x' + y )' = x . y'
  //   b) ( x' + y' ) + ( x . y ) = 1
  //   c) ( x . y )' . ( x + y' ) = y'
  //   d) ( x' . y )' + ( x + y' )' = 1
  //   e) ( y + x' + z' ) . ( y' + x + z )' = y . x' . z'
endmodule

module Guia_0403 (
  input  x,
  input  y,
  input  w,
  input  z,
  output a,
  output b,
  output c,
  output d,
  output e
);

  wire n1, n2, n3, n4, n5, n6, n7, n8, n9, n10, n11, n12, n13, n14, n15, n16, n17, n18, n19, n20, n21, n22,
       n23, n24, n25, n26, n27, n28, n29, n30, n31, n32, n33, n34, n35, n36, n37, n38, n39, n40, n41, n42,
       n43, n44, n45, n46, n47, n48, n49, n50, n51, n52, n53, n54, n55, n56, n57, n58, n59, n60, n61, n62,
       n63, n64, n65, n66, n67, n68, n69, n70, n71, n72, n73, n74, n75, n76, n77, n78, n79, n80, n81, n82,
       n83, n84, n85, n86, n87, n88, n89, n90, n91, n92, n93, n94, nw, nx, ny, nz;

  not not_1 (nx, x);
  not not_2 (ny, y);
  not not_3 (nw, w);
  not not_4 (nz, z);
  and and_1 (n1, nx, ny);
  and and_2 (n3, nx, y);
  and and_3 (n5, x, ny);
  and and_4 (n7, x, y);
  and and_5 (n11, nx, y);
  and and_6 (n13, nx, y);
  and and_7 (n15, x, ny);
  and and_8 (n17, x, y);
  and and_9 (n21, nx, ny);
  and and_10 (n24, nx, ny);
  and and_11 (n27, nx, y);
  and and_12 (n30, nx, y);
  and and_13 (n33, nx, y);
  and and_14 (n36, x, y);
  and and_15 (n39, x, y);
  and and_16 (n47, nx, ny);
  and and_17 (n50, nx, ny);
  and and_18 (n53, nx, y);
  and and_19 (n56, nx, y);
  and and_20 (n59, x, y);
  and and_21 (n62, x, y);
  and and_22 (n65, x, y);
  and and_23 (n73, nx, ny);
  and and_24 (n76, nx, ny);
  and and_25 (n79, x, ny);
  and and_26 (n82, x, ny);
  and and_27 (n85, x, y);
  and and_28 (n88, x, y);
  and and_29 (n2, n1, z);
  and and_30 (n4, n3, z);
  and and_31 (n6, n5, nz);
  and and_32 (n8, n7, z);
  and and_33 (n12, n11, nz);
  and and_34 (n14, n13, z);
  and and_35 (n16, n15, z);
  and and_36 (n18, n17, nz);
  and and_37 (n22, n21, nw);
  and and_38 (n25, n24, w);
  and and_39 (n28, n27, nw);
  and and_40 (n31, n30, w);
  and and_41 (n34, n33, w);
  and and_42 (n37, n36, nw);
  and and_43 (n40, n39, w);
  and and_44 (n48, n47, nw);
  and and_45 (n51, n50, w);
  and and_46 (n54, n53, nw);
  and and_47 (n57, n56, w);
  and and_48 (n60, n59, nw);
  and and_49 (n63, n62, nw);
  and and_50 (n66, n65, w);
  and and_51 (n74, n73, nw);
  and and_52 (n77, n76, nw);
  and and_53 (n80, n79, nw);
  and and_54 (n83, n82, nw);
  and and_55 (n86, n85, nw);
  and and_56 (n89, n88, w);
  and and_57 (n23, n22, z);
  and and_58 (n26, n25, nz);
  and and_59 (n29, n28, nz);
  and and_60 (n32, n31, nz);
  and and_61 (n35, n34, z);
  and and_62 (n38, n37, z);
  and and_63 (n41, n40, z);
  and and_64 (n49, n48, nz);
  and and_65 (n52, n51, nz);
  and and_66 (n55, n54, nz);
  and and_67 (n58, n57, nz);
  and and_68 (n61, n60, nz);
  and and_69 (n64, n63, z);
  and and_70 (n67, n66, nz);
  and and_71 (n75, n74, nz);
  and and_72 (n78, n77, z);
  and and_73 (n81, n80, nz);
  and and_74 (n84, n83, z);
  and and_75 (n87, n86, nz);
  and and_76 (n90, n89, z);
  or or_1 (n9, n2, n4);
  or or_2 (n19, n12, n14);
  or or_3 (n42, n23, n26);
  or or_4 (n68, n49, n52);
  or or_5 (n91, n75, n78);
  or or_6 (n10, n9, n6);
  or or_7 (n20, n19, n16);
  or or_8 (n43, n42, n29);
  or or_9 (n69, n68, n55);
  or or_10 (n92, n91, n81);
  or or_11 (a, n10, n8);
  or or_12 (b, n20, n18);
  or or_13 (n44, n43, n32);
  or or_14 (n70, n69, n58);
  or or_15 (n93, n92, n84);
  or or_16 (n45, n44, n35);
  or or_17 (n71, n70, n61);
  or or_18 (n94, n93, n87);
  or or_19 (n46, n45, n38);
  or or_20 (n72, n71, n64);
  or or_21 (e, n94, n90);
  or or_22 (c, n46, n41);
  or or_23 (d, n72, n67);

  // Other names for the same wires on the sheet: s_a = a; s_b = b; s_c = c; s_d = d; s_e = e

  // Notes on the sheet:
  //   Guia_0403 - Somas de produtos (SoP / mintermos)
  //   a) SoP(1,3,4,7)
  //   m1
  //   m3
  //   m4
  //   m7
  //   b) SoP(2,3,5,6)
  //   m2
  //   m3
  //   m5
  //   m6
  //   c) SoP(1,2,4,6,7,13,15)
  //   m1
  //   m2
  //   m4
  //   m6
  //   m7
  //   m13
  //   m15
  //   d) SoP(0,2,4,6,12,13,14)
  //   m0
  //   m2
  //   m4
  //   m6
  //   m12
  //   m13
  //   m14
  //   e) SoP(0,1,8,9,12,15)
  //   m0
  //   m1
  //   m8
  //   m9
  //   m12
  //   m15
endmodule

module Guia_0404 (
  input  x,
  input  y,
  input  w,
  input  z,
  output a,
  output b,
  output c,
  output d,
  output e
);

  wire n1, n2, n3, n4, n5, n6, n7, n8, n9, n10, n11, n12, n13, n14, n15, n16, n17, n18, n19, n20, n21, n22,
       n23, n24, n25, n26, n27, n28, n29, n30, n31, n32, n33, n34, n35, n36, n37, n38, n39, n40, n41, n42,
       n43, n44, n45, n46, n47, n48, n49, n50, n51, n52, n53, n54, n55, n56, n57, n58, n59, n60, n61, n62,
       n63, n64, n65, n66, n67, n68, n69, n70, n71, n72, n73, n74, n75, n76, n77, n78, n79, n80, n81, n82,
       n83, n84, n85, n86, n87, n88, n89, n90, n91, n92, n93, n94, n95, n96, n97, n98, n99, n100, n101, n102,
       nw, nx, ny, nz;

  not not_1 (nx, x);
  not not_2 (ny, y);
  not not_3 (nw, w);
  not not_4 (nz, z);
  or or_1 (n1, x, y);
  or or_2 (n3, x, ny);
  or or_3 (n5, nx, y);
  or or_4 (n7, nx, ny);
  or or_5 (n11, x, y);
  or or_6 (n13, x, ny);
  or or_7 (n15, x, ny);
  or or_8 (n17, nx, ny);
  or or_9 (n21, x, y);
  or or_10 (n24, x, y);
  or or_11 (n27, x, y);
  or or_12 (n30, x, ny);
  or or_13 (n33, x, ny);
  or or_14 (n36, nx, y);
  or or_15 (n39, nx, y);
  or or_16 (n42, nx, ny);
  or or_17 (n51, x, y);
  or or_18 (n54, x, y);
  or or_19 (n57, x, ny);
  or or_20 (n60, x, ny);
  or or_21 (n63, nx, y);
  or or_22 (n66, nx, ny);
  or or_23 (n69, nx, ny);
  or or_24 (n77, x, y);
  or or_25 (n80, x, y);
  or or_26 (n83, x, y);
  or or_27 (n86, x, ny);
  or or_28 (n89, x, ny);
  or or_29 (n92, nx, ny);
  or or_30 (n95, nx, ny);
  or or_31 (n2, n1, nz);
  or or_32 (n4, n3, z);
  or or_33 (n6, n5, z);
  or or_34 (n8, n7, z);
  or or_35 (n12, n11, z);
  or or_36 (n14, n13, z);
  or or_37 (n16, n15, nz);
  or or_38 (n18, n17, nz);
  or or_39 (n22, n21, w);
  or or_40 (n25, n24, w);
  or or_41 (n28, n27, nw);
  or or_42 (n31, n30, nw);
  or or_43 (n34, n33, nw);
  or or_44 (n37, n36, w);
  or or_45 (n40, n39, nw);
  or or_46 (n43, n42, w);
  or or_47 (n52, n51, w);
  or or_48 (n55, n54, nw);
  or or_49 (n58, n57, w);
  or or_50 (n61, n60, nw);
  or or_51 (n64, n63, w);
  or or_52 (n67, n66, w);
  or or_53 (n70, n69, nw);
  or or_54 (n78, n77, w);
  or or_55 (n81, n80, w);
  or or_56 (n84, n83, nw);
  or or_57 (n87, n86, w);
  or or_58 (n90, n89, nw);
  or or_59 (n93, n92, w);
  or or_60 (n96, n95, nw);
  or or_61 (n23, n22, z);
  or or_62 (n26, n25, nz);
  or or_63 (n29, n28, z);
  or or_64 (n32, n31, z);
  or or_65 (n35, n34, nz);
  or or_66 (n38, n37, z);
  or or_67 (n41, n40, nz);
  or or_68 (n44, n43, nz);
  or or_69 (n53, n52, nz);
  or or_70 (n56, n55, z);
  or or_71 (n59, n58, z);
  or or_72 (n62, n61, z);
  or or_73 (n65, n64, z);
  or or_74 (n68, n67, z);
  or or_75 (n71, n70, z);
  or or_76 (n79, n78, z);
  or or_77 (n82, n81, nz);
  or or_78 (n85, n84, z);
  or or_79 (n88, n87, z);
  or or_80 (n91, n90, nz);
  or or_81 (n94, n93, z);
  or or_82 (n97, n96, nz);
  and and_1 (n9, n2, n4);
  and and_2 (n19, n12, n14);
  and and_3 (n45, n23, n26);
  and and_4 (n72, n53, n56);
  and and_5 (n98, n79, n82);
  and and_6 (n10, n9, n6);
  and and_7 (n20, n19, n16);
  and and_8 (n46, n45, n29);
  and and_9 (n73, n72, n59);
  and and_10 (n99, n98, n85);
  and and_11 (a, n10, n8);
  and and_12 (b, n20, n18);
  and and_13 (n47, n46, n32);
  and and_14 (n74, n73, n62);
  and and_15 (n100, n99, n88);
  and and_16 (n48, n47, n35);
  and and_17 (n75, n74, n65);
  and and_18 (n101, n100, n91);
  and and_19 (n49, n48, n38);
  and and_20 (n76, n75, n68);
  and and_21 (n102, n101, n94);
  and and_22 (n50, n49, n41);
  and and_23 (d, n76, n71);
  and and_24 (e, n102, n97);
  and and_25 (c, n50, n44);

  // Other names for the same wires on the sheet: s_a = a; s_b = b; s_c = c; s_d = d; s_e = e

  // Notes on the sheet:
  //   Guia_0404 - Produtos de somas (PoS / MAXTERMOS)
  //   a) PoS(1,2,4,6)
  //   M1
  //   M2
  //   M4
  //   M6
  //   b) PoS(0,2,3,7)
  //   M0
  //   M2
  //   M3
  //   M7
  //   c) PoS(0,1,2,6,7,8,11,13)
  //   M0
  //   M1
  //   M2
  //   M6
  //   M7
  //   M8
  //   M11
  //   M13
  //   d) PoS(1,2,4,6,8,12,14)
  //   M1
  //   M2
  //   M4
  //   M6
  //   M8
  //   M12
  //   M14
  //   e) PoS(0,1,2,4,7,12,15)
  //   M0
  //   M1
  //   M2
  //   M4
  //   M7
  //   M12
  //   M15
endmodule
