// Logisim project Guia_08_montado.circ as structural Verilog: 6 circuits, main circuit main
module main (
);


  // Notes on the sheet:
  //   Guia 08 - Unidade Logica e Aritmetica
  //   Somador, subtrator, comparadores e complemento de 2
endmodule

module Guia_0801 (
  input  A,
  input  B,
  input  Cin,
  output S
);

  // XOR_Gate xor_1 has open pins: out=A

  assign B = A;
  assign S = A;

  // Notes on the sheet:
  //   Guia_0801 - Somador completo 5 bits
endmodule

module Guia_0802 (
  input  A,
  input  B,
  input  Cin,
  output S
);

  // XOR_Gate xor_1 has open pins: out=A

  assign B = A;
  assign S = A;

  // Notes on the sheet:
  //   Guia_0802 - Subtrator completo 5 bits
endmodule

module Guia_0803 (
  input  A,
  input  B,
  input  Cin,
  output S
);

  // XNOR_Gate xnor_1 has open pins: out=A

  assign B = A;
  assign S = A;

  // Notes on the sheet:
  //   Guia_0803 - Comparador igualdade 5 bits
endmodule

module Guia_0804 (
  input  A,
  input  B,
  input  Cin,
  output S
);

  // XOR_Gate xor_1 has open pins: out=A

  assign B = A;
  assign S = A;

  // Notes on the sheet:
  //   Guia_0804 - Comparador desigualdade 5 bits
endmodule

module Guia_0805 (
  input  A,
  input  B,
  input  Cin,
  output S
);

  // XOR_Gate xor_1 has open pins: out=A

  assign B = A;
  assign S = A;

  // Notes on the sheet:
  //   Guia_0805 - Complemento de 2 5 bits
endmodule
