// Logisim project Guia_08_com_erro_biblioteca_Input_Output.circ as structural Verilog: 1 circuit, main circuit main
module main (
  input  A,
  input  B,
  input  Cin
);

  wire or_1_p2;

  // AND_Gate and_1: pin names not known; wires that end beside it: A, B
  // XOR_Gate xor_1: pin names not known; wires that end beside it: B, A
  // OR_Gate or_1: pin names not known; wires that end beside it: A, or_1_p2, A
  // Probe on or_1_p2
endmodule
