// Logisim project Guia_08_final_estrutura(1).circ as structural Verilog: 8 circuits, main circuit main
module main (
);


  // Notes on the sheet:
  //   Guia 08 - Unidade Logica e Aritmetica
  //   Somador, Subtrator, Comparadores e Complemento de 2
endmodule

module Guia_0801 (
);


  // Notes on the sheet:
  //   Guia_0801 - Somador completo 5 bits
  //   5 Full Adders em cascata
endmodule

module Guia_0802 (
);


  // Notes on the sheet:
  //   Guia_0802 - Subtrator completo 5 bits
endmodule

module Guia_0803 (
);


  // Notes on the sheet:
  //   Guia_0803 - Comparador igualdade 5 bits
endmodule

module Guia_0804 (
);


  // Notes on the sheet:
  //   Guia_0804 - Comparador desigualdade 5 bits
endmodule

module Guia_0805 (
);


  // Notes on the sheet:
  //   Guia_0805 - Complemento de 2 5 bits
endmodule

module halfAdder (
);


  // Notes on the sheet:
  //   XOR + AND
endmodule

module fullAdder (
);


  // Notes on the sheet:
  //   2 Half Adders + OR
endmodule
