// Logisim project Guia_08.circ as structural Verilog
module Guia_08 (
  input  [4:0] ENTRADAS_5_BITS,
  output [4:0] SAIDA_5_BITS
);


  // Notes on the sheet:
  //   Guia 08 - Arquitetura de Computadores I - Matricula 897891
endmodule
