// Logisim project Guia_08_SomadorCompleto_Logisim.circ as structural Verilog: 1 circuit, main circuit main
module main (
  input  A,
  input  B,
  input  Cin
);

  // XOR_Gate xor_1 has open pins: out=A
  // XOR_Gate xor_2: pin names not known; wires that end beside it: A
  // AND_Gate and_1: pin names not known; wires that end beside it: A
  // AND_Gate and_2: pin names not known; wires that end beside it: A
  // OR_Gate or_1 has open pins: out=A
  // Probe on A
  // Probe on A

  assign B = A;
  assign Cin = A;
endmodule
