// Logisim project Guia_06.circ as structural Verilog: 7 circuits, main circuit main
module main (
);


  // Notes on the sheet:
  //   Guia 06 - Karnaugh, circuito completo e circuito simplificado
  //   Matricula: 897891   Nome: Lucas Junio Quirino Teixeira
  //   Abra Guia_0601 a Guia_0606 no painel esquerdo.
  //   Nas questoes 01-04: O = forma canonica/original; S = forma simplificada.
  //   Nas questoes 05-06: circuito fornecido no enunciado e circuito simplificado.
endmodule

module Guia_0601 (
  input  x,
  input  y,
  input  z,
  output a_S,
  output a_O,
  output b_S,
  output b_O,
  output c_S,
  output c_O,
  output d_S,
  output d_O,
  output e_S,
  output e_O
);

  wire _601ao_g1, _601ao_g2, _601ao_g3, _601ao_g4, _601ao_g5, _601ao_g6, _601ao_o7, _601as_g1, _601as_g2,
       _601as_g3, _601bo_g1, _601bo_g2, _601bo_g3, _601bo_g4, _601bo_g5, _601bo_g6, _601bo_o7, _601bs_g1,
       _601bs_g2, _601co_g1, _601co_g2, _601co_g3, _601co_g4, _601co_g5, _601co_g6, _601co_g7, _601co_g8,
       _601co_o9, _601co_o10, _601cs_g1, _601cs_g2, _601do_g1, _601do_g2, _601do_g3, _601do_g4, _601do_g5,
       _601do_g6, _601do_g7, _601do_g8, _601do_o9, _601do_o10, _601ds_g1, _601ds_g2, _601ds_g3, _601ds_g4,
       _601ds_o5, _601eo_g1, _601eo_g2, _601eo_g3, _601eo_g4, _601eo_g5, _601eo_g6, _601eo_g7, _601eo_g8,
       _601eo_o9, _601eo_o10, _601es_g1, _601es_g2, nx, ny, nz;

  and and_1 (_601ao_g1, nx, ny);
  and and_2 (_601ao_g3, x, y);
  and and_3 (_601ao_g5, x, y);
  and and_4 (_601bo_g1, nx, ny);
  and and_5 (_601bo_g3, nx, y);
  and and_6 (_601bo_g5, x, y);
  and and_7 (_601co_g1, nx, ny);
  and and_8 (_601co_g3, nx, y);
  and and_9 (_601co_g5, x, y);
  and and_10 (_601co_g7, x, y);
  and and_11 (_601do_g1, nx, ny);
  and and_12 (_601do_g3, nx, y);
  and and_13 (_601do_g5, x, ny);
  and and_14 (_601do_g7, x, y);
  and and_15 (_601eo_g1, nx, ny);
  and and_16 (_601eo_g3, nx, ny);
  and and_17 (_601eo_g5, x, ny);
  and and_18 (_601eo_g7, x, y);
  not not_1 (nx, x);
  not not_2 (ny, y);
  not not_3 (nz, z);
  and and_19 (_601ao_g2, _601ao_g1, z);
  and and_20 (_601ao_g4, _601ao_g3, nz);
  and and_21 (_601ao_g6, _601ao_g5, z);
  and and_22 (_601bo_g2, _601bo_g1, nz);
  and and_23 (_601bo_g4, _601bo_g3, nz);
  and and_24 (_601bo_g6, _601bo_g5, nz);
  and and_25 (_601co_g2, _601co_g1, z);
  and and_26 (_601co_g4, _601co_g3, z);
  and and_27 (_601co_g6, _601co_g5, nz);
  and and_28 (_601co_g8, _601co_g7, z);
  and and_29 (_601do_g2, _601do_g1, z);
  and and_30 (_601do_g4, _601do_g3, nz);
  and and_31 (_601do_g6, _601do_g5, nz);
  and and_32 (_601do_g8, _601do_g7, nz);
  and and_33 (_601eo_g2, _601eo_g1, nz);
  and and_34 (_601eo_g4, _601eo_g3, z);
  and and_35 (_601eo_g6, _601eo_g5, z);
  and and_36 (_601eo_g8, _601eo_g7, z);
  or or_1 (_601ao_o7, _601ao_g2, _601ao_g4);
  or or_2 (a_O, _601ao_o7, _601ao_g6);
  or or_3 (_601bo_o7, _601bo_g2, _601bo_g4);
  or or_4 (b_O, _601bo_o7, _601bo_g6);
  or or_5 (_601co_o9, _601co_g2, _601co_g4);
  or or_6 (_601co_o10, _601co_o9, _601co_g6);
  or or_7 (c_O, _601co_o10, _601co_g8);
  or or_8 (_601do_o9, _601do_g2, _601do_g4);
  or or_9 (_601do_o10, _601do_o9, _601do_g6);
  or or_10 (d_O, _601do_o10, _601do_g8);
  or or_11 (_601eo_o9, _601eo_g2, _601eo_g4);
  or or_12 (_601eo_o10, _601eo_o9, _601eo_g6);
  or or_13 (e_O, _601eo_o10, _601eo_g8);
  and and_37 (_601as_g1, x, y);
  and and_38 (_601as_g2, nx, ny);
  and and_39 (_601bs_g1, nx, nz);
  and and_40 (_601bs_g2, y, nz);
  and and_41 (_601cs_g1, nx, z);
  and and_42 (_601cs_g2, x, y);
  and and_43 (_601ds_g1, y, nz);
  and and_44 (_601ds_g2, x, nz);
  and and_45 (_601ds_g3, nx, ny);
  and and_46 (_601es_g1, nx, ny);
  and and_47 (_601es_g2, x, z);
  and and_48 (_601as_g3, _601as_g2, z);
  and and_49 (_601ds_g4, _601ds_g3, z);
  or or_14 (a_S, _601as_g1, _601as_g3);
  or or_15 (b_S, _601bs_g1, _601bs_g2);
  or or_16 (c_S, _601cs_g1, _601cs_g2);
  or or_17 (_601ds_o5, _601ds_g1, _601ds_g2);
  or or_18 (d_S, _601ds_o5, _601ds_g4);
  or or_19 (e_S, _601es_g1, _601es_g2);

  // Other names for the same wires on the sheet: _601ao_o8 = a_O; _601as_o4 = a_S; _601bo_o8 = b_O; _601bs_o3 = b_S;
  //   _601co_o11 = c_O; _601cs_o3 = c_S; _601do_o11 = d_O; _601ds_o6 = d_S; _601eo_o11 = e_O; _601es_o3 = e_S

  // Notes on the sheet:
  //   Guia_0601 - Mintermos, Karnaugh e simplificacao
  //   a) Sum m(1,6,7)    =>    x.y + x'.y'.z
  //   ORIGINAL / CANONICA
  //   b) Sum m(0,2,6)    =>    x'.z' + y.z'
  //   ORIGINAL / CANONICA
  //   c) Sum m(1,3,6,7)    =>    x'.z + x.y
  //   ORIGINAL / CANONICA
  //   d) Sum m(1,2,4,6)    =>    y.z' + x.z' + x'.y'.z
  //   ORIGINAL / CANONICA
  //   e) Sum m(0,1,5,7)    =>    x'.y' + x.z
  //   ORIGINAL / CANONICA
  //   SIMPLIFICADA
  //   SIMPLIFICADA
  //   SIMPLIFICADA
  //   SIMPLIFICADA
  //   SIMPLIFICADA
endmodule

module Guia_0602 (
  input  x,
  input  y,
  input  z,
  output a_S,
  output a_O,
  output b_S,
  output b_O,
  output c_S,
  output c_O,
  output d_S,
  output d_O,
  output e_S,
  output e_O
);

  wire _602ao_g1, _602ao_g2, _602ao_g3, _602ao_g4, _602ao_g5, _602ao_g6, _602ao_o7, _602as_g1, _602as_g2,
       _602bo_g1, _602bo_g2, _602bo_g3, _602bo_g4, _602bo_g5, _602bo_g6, _602bo_o7, _602bs_g1, _602bs_g2,
       _602co_g1, _602co_g2, _602co_g3, _602co_g4, _602co_g5, _602co_g6, _602co_g7, _602co_g8, _602co_o9,
       _602co_o10, _602cs_g1, _602cs_g2, _602do_g1, _602do_g2, _602do_g3, _602do_g4, _602do_g5, _602do_g6,
       _602do_g7, _602do_g8, _602do_o9, _602do_o10, _602ds_g1, _602ds_g2, _602ds_g3, _602ds_o4, _602eo_g1,
       _602eo_g2, _602eo_g3, _602eo_g4, _602eo_g5, _602eo_g6, _602eo_g7, _602eo_g8, _602eo_o9, _602eo_o10,
       _602es_g1, _602es_g2, nx, ny, nz;

  or or_1 (_602ao_g1, x, y);
  or or_2 (_602ao_g3, nx, y);
  or or_3 (_602ao_g5, nx, y);
  or or_4 (_602bo_g1, x, y);
  or or_5 (_602bo_g3, x, y);
  or or_6 (_602bo_g5, nx, y);
  or or_7 (_602co_g1, x, y);
  or or_8 (_602co_g3, x, ny);
  or or_9 (_602co_g5, x, ny);
  or or_10 (_602co_g7, nx, ny);
  or or_11 (_602do_g1, x, y);
  or or_12 (_602do_g3, x, y);
  or or_13 (_602do_g5, x, ny);
  or or_14 (_602do_g7, nx, y);
  or or_15 (_602eo_g1, x, y);
  or or_16 (_602eo_g3, x, y);
  or or_17 (_602eo_g5, nx, ny);
  or or_18 (_602eo_g7, nx, ny);
  not not_1 (nx, x);
  not not_2 (ny, y);
  not not_3 (nz, z);
  or or_19 (_602ao_g2, _602ao_g1, z);
  or or_20 (_602ao_g4, _602ao_g3, z);
  or or_21 (_602ao_g6, _602ao_g5, nz);
  or or_22 (_602bo_g2, _602bo_g1, z);
  or or_23 (_602bo_g4, _602bo_g3, nz);
  or or_24 (_602bo_g6, _602bo_g5, nz);
  or or_25 (_602co_g2, _602co_g1, nz);
  or or_26 (_602co_g4, _602co_g3, z);
  or or_27 (_602co_g6, _602co_g5, nz);
  or or_28 (_602co_g8, _602co_g7, z);
  or or_29 (_602do_g2, _602do_g1, z);
  or or_30 (_602do_g4, _602do_g3, nz);
  or or_31 (_602do_g6, _602do_g5, nz);
  or or_32 (_602do_g8, _602do_g7, nz);
  or or_33 (_602eo_g2, _602eo_g1, z);
  or or_34 (_602eo_g4, _602eo_g3, nz);
  or or_35 (_602eo_g6, _602eo_g5, z);
  or or_36 (_602eo_g8, _602eo_g7, nz);
  and and_1 (_602ao_o7, _602ao_g2, _602ao_g4);
  and and_2 (a_O, _602ao_o7, _602ao_g6);
  and and_3 (_602bo_o7, _602bo_g2, _602bo_g4);
  and and_4 (b_O, _602bo_o7, _602bo_g6);
  and and_5 (_602co_o9, _602co_g2, _602co_g4);
  and and_6 (_602co_o10, _602co_o9, _602co_g6);
  and and_7 (c_O, _602co_o10, _602co_g8);
  and and_8 (_602do_o9, _602do_g2, _602do_g4);
  and and_9 (_602do_o10, _602do_o9, _602do_g6);
  and and_10 (d_O, _602do_o10, _602do_g8);
  and and_11 (_602eo_o9, _602eo_g2, _602eo_g4);
  and and_12 (_602eo_o10, _602eo_o9, _602eo_g6);
  and and_13 (e_O, _602eo_o10, _602eo_g8);
  or or_37 (_602as_g1, y, z);
  or or_38 (_602as_g2, y, nx);
  or or_39 (_602bs_g1, x, y);
  or or_40 (_602bs_g2, y, nz);
  or or_41 (_602cs_g1, x, nz);
  or or_42 (_602cs_g2, z, ny);
  or or_43 (_602ds_g1, x, y);
  or or_44 (_602ds_g2, x, nz);
  or or_45 (_602ds_g3, y, nz);
  or or_46 (_602es_g1, x, y);
  or or_47 (_602es_g2, nx, ny);
  and and_14 (a_S, _602as_g1, _602as_g2);
  and and_15 (b_S, _602bs_g1, _602bs_g2);
  and and_16 (c_S, _602cs_g1, _602cs_g2);
  and and_17 (_602ds_o4, _602ds_g1, _602ds_g2);
  and and_18 (d_S, _602ds_o4, _602ds_g3);
  and and_19 (e_S, _602es_g1, _602es_g2);

  // Other names for the same wires on the sheet: _602ao_o8 = a_O; _602as_o3 = a_S; _602bo_o8 = b_O; _602bs_o3 = b_S;
  //   _602co_o11 = c_O; _602cs_o3 = c_S; _602do_o11 = d_O; _602ds_o5 = d_S; _602eo_o11 = e_O; _602es_o3 = e_S

  // Notes on the sheet:
  //   Guia_0602 - Maxtermos, Karnaugh e simplificacao
  //   a) Pi M(0,4,5)    =>    (Y+Z).(Y+X')
  //   ORIGINAL / CANONICA
  //   b) Pi M(0,1,5)    =>    (X+Y).(Y+Z')
  //   ORIGINAL / CANONICA
  //   c) Pi M(1,2,3,6)    =>    (X+Z').(Z+Y')
  //   ORIGINAL / CANONICA
  //   d) Pi M(0,1,3,5)    =>    (X+Y).(X+Z').(Y+Z')
  //   ORIGINAL / CANONICA
  //   e) Pi M(0,1,6,7)    =>    (X+Y).(X'+Y')
  //   ORIGINAL / CANONICA
  //   SIMPLIFICADA
  //   SIMPLIFICADA
  //   SIMPLIFICADA
  //   SIMPLIFICADA
  //   SIMPLIFICADA
endmodule

module Guia_0603 (
  input  x,
  input  y,
  input  w,
  input  z,
  output a_S,
  output a_O,
  output b_S,
  output b_O,
  output c_S,
  output c_O,
  output d_S,
  output d_O,
  output e_S,
  output e_O
);

  wire _603ao_g1, _603ao_g2, _603ao_g3, _603ao_g4, _603ao_g5, _603ao_g6, _603ao_g7, _603ao_g8, _603ao_g9,
       _603ao_g10, _603ao_g11, _603ao_g12, _603ao_g13, _603ao_g14, _603ao_g15, _603ao_g16, _603ao_g17,
       _603ao_g18, _603ao_o19, _603ao_o20, _603ao_o21, _603ao_o22, _603as_g1, _603as_g2, _603as_g3,
       _603as_g4, _603as_g5, _603as_g6, _603as_g7, _603as_g8, _603as_g9, _603as_o10, _603as_o11, _603bo_g1,
       _603bo_g2, _603bo_g3, _603bo_g4, _603bo_g5, _603bo_g6, _603bo_g7, _603bo_g8, _603bo_g9, _603bo_g10,
       _603bo_g11, _603bo_g12, _603bo_g13, _603bo_g14, _603bo_g15, _603bo_g16, _603bo_g17, _603bo_g18,
       _603bo_g19, _603bo_g20, _603bo_g21, _603bo_o22, _603bo_o23, _603bo_o24, _603bo_o25, _603bo_o26,
       _603bs_g1, _603bs_g2, _603bs_g3, _603bs_g4, _603bs_g5, _603bs_g6, _603bs_g7, _603bs_o8, _603bs_o9,
       _603co_g1, _603co_g2, _603co_g3, _603co_g4, _603co_g5, _603co_g6, _603co_g7, _603co_g8, _603co_g9,
       _603co_g10, _603co_g11, _603co_g12, _603co_g13, _603co_g14, _603co_g15, _603co_g16, _603co_g17,
       _603co_g18, _603co_g19, _603co_g20, _603co_g21, _603co_g22, _603co_g23, _603co_g24, _603co_o25,
       _603co_o26, _603co_o27, _603co_o28, _603co_o29, _603co_o30, _603cs_g1, _603cs_g2, _603cs_g3,
       _603cs_g4, _603cs_g5, _603cs_g6, _603cs_g7, _603cs_g8, _603cs_g9, _603cs_g10, _603cs_o11, _603cs_o12,
       _603cs_o13, _603do_g1, _603do_g2, _603do_g3, _603do_g4, _603do_g5, _603do_g6, _603do_g7, _603do_g8,
       _603do_g9, _603do_g10, _603do_g11, _603do_g12, _603do_g13, _603do_g14, _603do_g15, _603do_g16,
       _603do_g17, _603do_g18, _603do_g19, _603do_g20, _603do_g21, _603do_o22, _603do_o23, _603do_o24,
       _603do_o25, _603do_o26, _603ds_g1, _603ds_g2, _603ds_g3, _603ds_g4, _603ds_g5, _603ds_g6, _603ds_g7,
       _603ds_g8, _603ds_o9, _603ds_o10, _603eo_g1, _603eo_g2, _603eo_g3, _603eo_g4, _603eo_g5, _603eo_g6,
       _603eo_g7, _603eo_g8, _603eo_g9, _603eo_g10, _603eo_g11, _603eo_g12, _603eo_g13, _603eo_g14,
       _603eo_g15, _603eo_g16, _603eo_g17, _603eo_g18, _603eo_g19, _603eo_g20, _603eo_g21, _603eo_g22,
       _603eo_g23, _603eo_g24, _603eo_o25, _603eo_o26, _603eo_o27, _603eo_o28, _603eo_o29, _603eo_o30,
       _603es_g1, _603es_g2, _603es_g3, _603es_g4, _603es_g5, _603es_g6, _603es_g7, _603es_o8, _603es_o9, nw,
       nx, ny, nz;

  and and_1 (_603ao_g1, nx, ny);
  and and_2 (_603ao_g4, nx, ny);
  and and_3 (_603ao_g7, nx, y);
  and and_4 (_603ao_g10, x, ny);
  and and_5 (_603ao_g13, x, y);
  and and_6 (_603ao_g16, x, y);
  and and_7 (_603bo_g1, nx, ny);
  and and_8 (_603bo_g4, nx, ny);
  and and_9 (_603bo_g7, nx, ny);
  and and_10 (_603bo_g10, nx, y);
  and and_11 (_603bo_g13, x, ny);
  and and_12 (_603bo_g16, x, y);
  and and_13 (_603bo_g19, x, y);
  and and_14 (_603co_g1, nx, ny);
  and and_15 (_603co_g4, nx, ny);
  and and_16 (_603co_g7, nx, ny);
  and and_17 (_603co_g10, nx, y);
  and and_18 (_603co_g13, x, ny);
  and and_19 (_603co_g16, x, ny);
  and and_20 (_603co_g19, x, y);
  and and_21 (_603co_g22, x, y);
  and and_22 (_603do_g1, nx, ny);
  and and_23 (_603do_g4, nx, ny);
  and and_24 (_603do_g7, nx, y);
  and and_25 (_603do_g10, nx, y);
  and and_26 (_603do_g13, x, ny);
  and and_27 (_603do_g16, x, y);
  and and_28 (_603do_g19, x, y);
  and and_29 (_603eo_g1, nx, ny);
  and and_30 (_603eo_g4, nx, ny);
  and and_31 (_603eo_g7, nx, ny);
  and and_32 (_603eo_g10, nx, y);
  and and_33 (_603eo_g13, nx, y);
  and and_34 (_603eo_g16, x, ny);
  and and_35 (_603eo_g19, x, ny);
  and and_36 (_603eo_g22, x, y);
  not not_1 (nx, x);
  not not_2 (ny, y);
  not not_3 (nw, w);
  not not_4 (nz, z);
  and and_37 (_603ao_g2, _603ao_g1, nw);
  and and_38 (_603ao_g5, _603ao_g4, w);
  and and_39 (_603ao_g8, _603ao_g7, nw);
  and and_40 (_603ao_g11, _603ao_g10, nw);
  and and_41 (_603ao_g14, _603ao_g13, nw);
  and and_42 (_603ao_g17, _603ao_g16, nw);
  and and_43 (_603bo_g2, _603bo_g1, nw);
  and and_44 (_603bo_g5, _603bo_g4, nw);
  and and_45 (_603bo_g8, _603bo_g7, w);
  and and_46 (_603bo_g11, _603bo_g10, nw);
  and and_47 (_603bo_g14, _603bo_g13, nw);
  and and_48 (_603bo_g17, _603bo_g16, nw);
  and and_49 (_603bo_g20, _603bo_g19, w);
  and and_50 (_603co_g2, _603co_g1, nw);
  and and_51 (_603co_g5, _603co_g4, nw);
  and and_52 (_603co_g8, _603co_g7, w);
  and and_53 (_603co_g11, _603co_g10, w);
  and and_54 (_603co_g14, _603co_g13, w);
  and and_55 (_603co_g17, _603co_g16, w);
  and and_56 (_603co_g20, _603co_g19, nw);
  and and_57 (_603co_g23, _603co_g22, w);
  and and_58 (_603do_g2, _603do_g1, w);
  and and_59 (_603do_g5, _603do_g4, w);
  and and_60 (_603do_g8, _603do_g7, nw);
  and and_61 (_603do_g11, _603do_g10, w);
  and and_62 (_603do_g14, _603do_g13, w);
  and and_63 (_603do_g17, _603do_g16, nw);
  and and_64 (_603do_g20, _603do_g19, w);
  and and_65 (_603eo_g2, _603eo_g1, nw);
  and and_66 (_603eo_g5, _603eo_g4, nw);
  and and_67 (_603eo_g8, _603eo_g7, w);
  and and_68 (_603eo_g11, _603eo_g10, nw);
  and and_69 (_603eo_g14, _603eo_g13, w);
  and and_70 (_603eo_g17, _603eo_g16, nw);
  and and_71 (_603eo_g20, _603eo_g19, w);
  and and_72 (_603eo_g23, _603eo_g22, nw);
  and and_73 (_603ao_g3, _603ao_g2, z);
  and and_74 (_603ao_g6, _603ao_g5, nz);
  and and_75 (_603ao_g9, _603ao_g8, z);
  and and_76 (_603ao_g12, _603ao_g11, nz);
  and and_77 (_603ao_g15, _603ao_g14, nz);
  and and_78 (_603ao_g18, _603ao_g17, z);
  and and_79 (_603bo_g3, _603bo_g2, nz);
  and and_80 (_603bo_g6, _603bo_g5, z);
  and and_81 (_603bo_g9, _603bo_g8, z);
  and and_82 (_603bo_g12, _603bo_g11, z);
  and and_83 (_603bo_g15, _603bo_g14, z);
  and and_84 (_603bo_g18, _603bo_g17, z);
  and and_85 (_603bo_g21, _603bo_g20, z);
  and and_86 (_603co_g3, _603co_g2, nz);
  and and_87 (_603co_g6, _603co_g5, z);
  and and_88 (_603co_g9, _603co_g8, nz);
  and and_89 (_603co_g12, _603co_g11, z);
  and and_90 (_603co_g15, _603co_g14, nz);
  and and_91 (_603co_g18, _603co_g17, z);
  and and_92 (_603co_g21, _603co_g20, z);
  and and_93 (_603co_g24, _603co_g23, z);
  and and_94 (_603do_g3, _603do_g2, nz);
  and and_95 (_603do_g6, _603do_g5, z);
  and and_96 (_603do_g9, _603do_g8, z);
  and and_97 (_603do_g12, _603do_g11, z);
  and and_98 (_603do_g15, _603do_g14, z);
  and and_99 (_603do_g18, _603do_g17, nz);
  and and_100 (_603do_g21, _603do_g20, z);
  and and_101 (_603eo_g3, _603eo_g2, nz);
  and and_102 (_603eo_g6, _603eo_g5, z);
  and and_103 (_603eo_g9, _603eo_g8, z);
  and and_104 (_603eo_g12, _603eo_g11, z);
  and and_105 (_603eo_g15, _603eo_g14, z);
  and and_106 (_603eo_g18, _603eo_g17, nz);
  and and_107 (_603eo_g21, _603eo_g20, z);
  and and_108 (_603eo_g24, _603eo_g23, z);
  or or_1 (_603ao_o19, _603ao_g3, _603ao_g6);
  or or_2 (_603ao_o20, _603ao_o19, _603ao_g9);
  or or_3 (_603ao_o21, _603ao_o20, _603ao_g12);
  or or_4 (_603ao_o22, _603ao_o21, _603ao_g15);
  or or_5 (a_O, _603ao_o22, _603ao_g18);
  or or_6 (_603bo_o22, _603bo_g3, _603bo_g6);
  or or_7 (_603bo_o23, _603bo_o22, _603bo_g9);
  or or_8 (_603bo_o24, _603bo_o23, _603bo_g12);
  or or_9 (_603bo_o25, _603bo_o24, _603bo_g15);
  or or_10 (_603bo_o26, _603bo_o25, _603bo_g18);
  or or_11 (b_O, _603bo_o26, _603bo_g21);
  or or_12 (_603co_o25, _603co_g3, _603co_g6);
  or or_13 (_603co_o26, _603co_o25, _603co_g9);
  or or_14 (_603co_o27, _603co_o26, _603co_g12);
  or or_15 (_603co_o28, _603co_o27, _603co_g15);
  or or_16 (_603co_o29, _603co_o28, _603co_g18);
  or or_17 (_603co_o30, _603co_o29, _603co_g21);
  or or_18 (c_O, _603co_o30, _603co_g24);
  or or_19 (_603do_o22, _603do_g3, _603do_g6);
  or or_20 (_603do_o23, _603do_o22, _603do_g9);
  or or_21 (_603do_o24, _603do_o23, _603do_g12);
  or or_22 (_603do_o25, _603do_o24, _603do_g15);
  or or_23 (_603do_o26, _603do_o25, _603do_g18);
  or or_24 (d_O, _603do_o26, _603do_g21);
  or or_25 (_603eo_o25, _603eo_g3, _603eo_g6);
  or or_26 (_603eo_o26, _603eo_o25, _603eo_g9);
  or or_27 (_603eo_o27, _603eo_o26, _603eo_g12);
  or or_28 (_603eo_o28, _603eo_o27, _603eo_g15);
  or or_29 (_603eo_o29, _603eo_o28, _603eo_g18);
  or or_30 (_603eo_o30, _603eo_o29, _603eo_g21);
  or or_31 (e_O, _603eo_o30, _603eo_g24);
  and and_109 (_603as_g1, y, z);
  and and_110 (_603as_g3, x, nw);
  and and_111 (_603as_g5, nx, z);
  and and_112 (_603as_g7, nx, ny);
  and and_113 (_603bs_g1, z, nw);
  and and_114 (_603bs_g2, x, y);
  and and_115 (_603bs_g4, nx, ny);
  and and_116 (_603bs_g6, nx, ny);
  and and_117 (_603cs_g1, y, w);
  and and_118 (_603cs_g3, x, y);
  and and_119 (_603cs_g5, x, ny);
  and and_120 (_603cs_g7, ny, w);
  and and_121 (_603cs_g9, nx, ny);
  and and_122 (_603ds_g1, w, z);
  and and_123 (_603ds_g2, nx, y);
  and and_124 (_603ds_g4, nx, ny);
  and and_125 (_603ds_g6, x, y);
  and and_126 (_603es_g1, nx, z);
  and and_127 (_603es_g2, ny, w);
  and and_128 (_603es_g4, y, nw);
  and and_129 (_603es_g6, ny, nw);
  and and_130 (_603as_g2, _603as_g1, nw);
  and and_131 (_603as_g4, _603as_g3, nz);
  and and_132 (_603as_g6, _603as_g5, nw);
  and and_133 (_603as_g8, _603as_g7, w);
  and and_134 (_603bs_g3, _603bs_g2, z);
  and and_135 (_603bs_g5, _603bs_g4, z);
  and and_136 (_603bs_g7, _603bs_g6, nw);
  and and_137 (_603cs_g2, _603cs_g1, z);
  and and_138 (_603cs_g4, _603cs_g3, z);
  and and_139 (_603cs_g6, _603cs_g5, w);
  and and_140 (_603cs_g8, _603cs_g7, nz);
  and and_141 (_603cs_g10, _603cs_g9, nw);
  and and_142 (_603ds_g3, _603ds_g2, z);
  and and_143 (_603ds_g5, _603ds_g4, w);
  and and_144 (_603ds_g7, _603ds_g6, nw);
  and and_145 (_603es_g3, _603es_g2, z);
  and and_146 (_603es_g5, _603es_g4, z);
  and and_147 (_603es_g7, _603es_g6, nz);
  and and_148 (_603as_g9, _603as_g8, nz);
  and and_149 (_603ds_g8, _603ds_g7, nz);
  or or_32 (_603as_o10, _603as_g2, _603as_g4);
  or or_33 (_603as_o11, _603as_o10, _603as_g6);
  or or_34 (a_S, _603as_o11, _603as_g9);
  or or_35 (_603bs_o8, _603bs_g1, _603bs_g3);
  or or_36 (_603bs_o9, _603bs_o8, _603bs_g5);
  or or_37 (b_S, _603bs_o9, _603bs_g7);
  or or_38 (_603cs_o11, _603cs_g2, _603cs_g4);
  or or_39 (_603cs_o12, _603cs_o11, _603cs_g6);
  or or_40 (_603cs_o13, _603cs_o12, _603cs_g8);
  or or_41 (c_S, _603cs_o13, _603cs_g10);
  or or_42 (_603ds_o9, _603ds_g1, _603ds_g3);
  or or_43 (_603ds_o10, _603ds_o9, _603ds_g5);
  or or_44 (d_S, _603ds_o10, _603ds_g8);
  or or_45 (_603es_o8, _603es_g1, _603es_g3);
  or or_46 (_603es_o9, _603es_o8, _603es_g5);
  or or_47 (e_S, _603es_o9, _603es_g7);

  // Other names for the same wires on the sheet: _603ao_o23 = a_O; _603as_o12 = a_S; _603bo_o27 = b_O;
  //   _603bs_o10 = b_S; _603co_o31 = c_O; _603cs_o14 = c_S; _603do_o27 = d_O; _603ds_o11 = d_S; _603eo_o31 = e_O;
  //   _603es_o10 = e_S

  // Notes on the sheet:
  //   Guia_0603 - Mintermos de 4 variaveis e simplificacao
  //   a) Sum m(1,2,5,8,12,13)
  //   Simplificada: y.z.w' + x.w'.z' + x'.z.w' + x'.y'.w.z'
  //   ORIGINAL / CANONICA
  //   b) Sum m(0,1,3,5,9,13,15)
  //   Simplificada: z.w' + x.y.z + x'.y'.z + x'.y'.w'
  //   ORIGINAL / CANONICA
  //   c) Sum m(0,1,2,7,10,11,13,15)
  //   Simplificada: y.w.z + x.y.z + x.y'.w + y'.w.z' + x'.y'.w'
  //   ORIGINAL / CANONICA
  //   d) Sum m(2,3,5,7,11,12,15)
  //   Simplificada: w.z + x'.y.z + x'.y'.w + x.y.w'.z'
  //   ORIGINAL / CANONICA
  //   e) Sum m(0,1,3,5,7,8,11,13)
  //   Simplificada: x'.z + y'.w.z + y.w'.z + y'.w'.z'
  //   ORIGINAL / CANONICA
  //   SIMPLIFICADA
  //   SIMPLIFICADA
  //   SIMPLIFICADA
  //   SIMPLIFICADA
  //   SIMPLIFICADA
endmodule

module Guia_0604 (
  input  x,
  input  y,
  input  w,
  input  z,
  output a_S,
  output a_O,
  output b_S,
  output b_O,
  output c_S,
  output c_O,
  output d_S,
  output d_O,
  output e_S,
  output e_O
);

  wire _604ao_g1, _604ao_g2, _604ao_g3, _604ao_g4, _604ao_g5, _604ao_g6, _604ao_g7, _604ao_g8, _604ao_g9,
       _604ao_g10, _604ao_g11, _604ao_g12, _604ao_o13, _604ao_o14, _604as_g1, _604as_g2, _604as_g3,
       _604as_g4, _604as_g5, _604as_g6, _604as_o7, _604bo_g1, _604bo_g2, _604bo_g3, _604bo_g4, _604bo_g5,
       _604bo_g6, _604bo_g7, _604bo_g8, _604bo_g9, _604bo_g10, _604bo_g11, _604bo_g12, _604bo_g13,
       _604bo_g14, _604bo_g15, _604bo_o16, _604bo_o17, _604bo_o18, _604bs_g1, _604bs_g2, _604bs_g3,
       _604bs_g4, _604bs_g5, _604bs_g6, _604bs_g7, _604bs_o8, _604co_g1, _604co_g2, _604co_g3, _604co_g4,
       _604co_g5, _604co_g6, _604co_g7, _604co_g8, _604co_g9, _604co_g10, _604co_g11, _604co_g12, _604co_g13,
       _604co_g14, _604co_g15, _604co_o16, _604co_o17, _604co_o18, _604cs_g1, _604cs_g2, _604cs_g3,
       _604cs_g4, _604cs_g5, _604cs_g6, _604cs_g7, _604cs_o8, _604do_g1, _604do_g2, _604do_g3, _604do_g4,
       _604do_g5, _604do_g6, _604do_g7, _604do_g8, _604do_g9, _604do_g10, _604do_g11, _604do_g12, _604do_g13,
       _604do_g14, _604do_g15, _604do_g16, _604do_g17, _604do_g18, _604do_o19, _604do_o20, _604do_o21,
       _604do_o22, _604ds_g1, _604ds_g2, _604ds_g3, _604ds_g4, _604ds_g5, _604ds_o6, _604eo_g1, _604eo_g2,
       _604eo_g3, _604eo_g4, _604eo_g5, _604eo_g6, _604eo_g7, _604eo_g8, _604eo_g9, _604eo_g10, _604eo_g11,
       _604eo_g12, _604eo_g13, _604eo_g14, _604eo_g15, _604eo_g16, _604eo_g17, _604eo_g18, _604eo_g19,
       _604eo_g20, _604eo_g21, _604eo_o22, _604eo_o23, _604eo_o24, _604eo_o25, _604eo_o26, _604es_g1,
       _604es_g2, _604es_g3, _604es_g4, _604es_g5, _604es_o6, nw, nx, ny, nz;

  or or_1 (_604ao_g1, x, y);
  or or_2 (_604ao_g4, x, ny);
  or or_3 (_604ao_g7, x, ny);
  or or_4 (_604ao_g10, nx, ny);
  or or_5 (_604bo_g1, x, ny);
  or or_6 (_604bo_g4, x, ny);
  or or_7 (_604bo_g7, nx, y);
  or or_8 (_604bo_g10, nx, ny);
  or or_9 (_604bo_g13, nx, ny);
  or or_10 (_604co_g1, x, ny);
  or or_11 (_604co_g4, x, ny);
  or or_12 (_604co_g7, nx, y);
  or or_13 (_604co_g10, nx, ny);
  or or_14 (_604co_g13, nx, ny);
  or or_15 (_604do_g1, x, y);
  or or_16 (_604do_g4, x, ny);
  or or_17 (_604do_g7, x, ny);
  or or_18 (_604do_g10, nx, ny);
  or or_19 (_604do_g13, nx, ny);
  or or_20 (_604do_g16, nx, ny);
  or or_21 (_604eo_g1, x, y);
  or or_22 (_604eo_g4, x, y);
  or or_23 (_604eo_g7, x, ny);
  or or_24 (_604eo_g10, x, ny);
  or or_25 (_604eo_g13, nx, y);
  or or_26 (_604eo_g16, nx, ny);
  or or_27 (_604eo_g19, nx, ny);
  not not_1 (nx, x);
  not not_2 (ny, y);
  not not_3 (nw, w);
  not not_4 (nz, z);
  or or_28 (_604ao_g2, _604ao_g1, nw);
  or or_29 (_604ao_g5, _604ao_g4, nw);
  or or_30 (_604ao_g8, _604ao_g7, nw);
  or or_31 (_604ao_g11, _604ao_g10, nw);
  or or_32 (_604bo_g2, _604bo_g1, w);
  or or_33 (_604bo_g5, _604bo_g4, nw);
  or or_34 (_604bo_g8, _604bo_g7, w);
  or or_35 (_604bo_g11, _604bo_g10, w);
  or or_36 (_604bo_g14, _604bo_g13, nw);
  or or_37 (_604co_g2, _604co_g1, w);
  or or_38 (_604co_g5, _604co_g4, nw);
  or or_39 (_604co_g8, _604co_g7, w);
  or or_40 (_604co_g11, _604co_g10, nw);
  or or_41 (_604co_g14, _604co_g13, nw);
  or or_42 (_604do_g2, _604do_g1, w);
  or or_43 (_604do_g5, _604do_g4, w);
  or or_44 (_604do_g8, _604do_g7, nw);
  or or_45 (_604do_g11, _604do_g10, w);
  or or_46 (_604do_g14, _604do_g13, w);
  or or_47 (_604do_g17, _604do_g16, nw);
  or or_48 (_604eo_g2, _604eo_g1, nw);
  or or_49 (_604eo_g5, _604eo_g4, nw);
  or or_50 (_604eo_g8, _604eo_g7, w);
  or or_51 (_604eo_g11, _604eo_g10, nw);
  or or_52 (_604eo_g14, _604eo_g13, nw);
  or or_53 (_604eo_g17, _604eo_g16, w);
  or or_54 (_604eo_g20, _604eo_g19, nw);
  or or_55 (_604ao_g3, _604ao_g2, z);
  or or_56 (_604ao_g6, _604ao_g5, z);
  or or_57 (_604ao_g9, _604ao_g8, nz);
  or or_58 (_604ao_g12, _604ao_g11, z);
  or or_59 (_604bo_g3, _604bo_g2, z);
  or or_60 (_604bo_g6, _604bo_g5, nz);
  or or_61 (_604bo_g9, _604bo_g8, nz);
  or or_62 (_604bo_g12, _604bo_g11, nz);
  or or_63 (_604bo_g15, _604bo_g14, nz);
  or or_64 (_604co_g3, _604co_g2, z);
  or or_65 (_604co_g6, _604co_g5, z);
  or or_66 (_604co_g9, _604co_g8, z);
  or or_67 (_604co_g12, _604co_g11, z);
  or or_68 (_604co_g15, _604co_g14, nz);
  or or_69 (_604do_g3, _604do_g2, nz);
  or or_70 (_604do_g6, _604do_g5, nz);
  or or_71 (_604do_g9, _604do_g8, nz);
  or or_72 (_604do_g12, _604do_g11, z);
  or or_73 (_604do_g15, _604do_g14, nz);
  or or_74 (_604do_g18, _604do_g17, nz);
  or or_75 (_604eo_g3, _604eo_g2, z);
  or or_76 (_604eo_g6, _604eo_g5, nz);
  or or_77 (_604eo_g9, _604eo_g8, z);
  or or_78 (_604eo_g12, _604eo_g11, z);
  or or_79 (_604eo_g15, _604eo_g14, nz);
  or or_80 (_604eo_g18, _604eo_g17, z);
  or or_81 (_604eo_g21, _604eo_g20, z);
  and and_1 (_604ao_o13, _604ao_g3, _604ao_g6);
  and and_2 (_604ao_o14, _604ao_o13, _604ao_g9);
  and and_3 (a_O, _604ao_o14, _604ao_g12);
  and and_4 (_604bo_o16, _604bo_g3, _604bo_g6);
  and and_5 (_604bo_o17, _604bo_o16, _604bo_g9);
  and and_6 (_604bo_o18, _604bo_o17, _604bo_g12);
  and and_7 (b_O, _604bo_o18, _604bo_g15);
  and and_8 (_604co_o16, _604co_g3, _604co_g6);
  and and_9 (_604co_o17, _604co_o16, _604co_g9);
  and and_10 (_604co_o18, _604co_o17, _604co_g12);
  and and_11 (c_O, _604co_o18, _604co_g15);
  and and_12 (_604do_o19, _604do_g3, _604do_g6);
  and and_13 (_604do_o20, _604do_o19, _604do_g9);
  and and_14 (_604do_o21, _604do_o20, _604do_g12);
  and and_15 (_604do_o22, _604do_o21, _604do_g15);
  and and_16 (d_O, _604do_o22, _604do_g18);
  and and_17 (_604eo_o22, _604eo_g3, _604eo_g6);
  and and_18 (_604eo_o23, _604eo_o22, _604eo_g9);
  and and_19 (_604eo_o24, _604eo_o23, _604eo_g12);
  and and_20 (_604eo_o25, _604eo_o24, _604eo_g15);
  and and_21 (_604eo_o26, _604eo_o25, _604eo_g18);
  and and_22 (e_O, _604eo_o26, _604eo_g21);
  or or_82 (_604as_g1, x, z);
  or or_83 (_604as_g3, x, nw);
  or or_84 (_604as_g5, z, nw);
  or or_85 (_604bs_g1, w, nx);
  or or_86 (_604bs_g3, w, x);
  or or_87 (_604bs_g6, nw, ny);
  or or_88 (_604cs_g1, x, z);
  or or_89 (_604cs_g3, w, y);
  or or_90 (_604cs_g6, nw, nx);
  or or_91 (_604ds_g1, ny, nz);
  or or_92 (_604ds_g2, w, x);
  or or_93 (_604ds_g4, w, nx);
  or or_94 (_604es_g1, z, ny);
  or or_95 (_604es_g2, x, y);
  or or_96 (_604es_g4, y, nw);
  or or_97 (_604as_g2, _604as_g1, nw);
  or or_98 (_604as_g4, _604as_g3, ny);
  or or_99 (_604as_g6, _604as_g5, ny);
  or or_100 (_604bs_g2, _604bs_g1, nz);
  or or_101 (_604bs_g4, _604bs_g3, z);
  or or_102 (_604bs_g7, _604bs_g6, nz);
  or or_103 (_604cs_g2, _604cs_g1, ny);
  or or_104 (_604cs_g4, _604cs_g3, z);
  or or_105 (_604cs_g7, _604cs_g6, ny);
  or or_106 (_604ds_g3, _604ds_g2, nz);
  or or_107 (_604ds_g5, _604ds_g4, ny);
  or or_108 (_604es_g3, _604es_g2, nw);
  or or_109 (_604es_g5, _604es_g4, nz);
  or or_110 (_604bs_g5, _604bs_g4, ny);
  or or_111 (_604cs_g5, _604cs_g4, nx);
  and and_23 (_604as_o7, _604as_g2, _604as_g4);
  and and_24 (a_S, _604as_o7, _604as_g6);
  and and_25 (_604bs_o8, _604bs_g2, _604bs_g5);
  and and_26 (b_S, _604bs_o8, _604bs_g7);
  and and_27 (_604cs_o8, _604cs_g2, _604cs_g5);
  and and_28 (c_S, _604cs_o8, _604cs_g7);
  and and_29 (_604ds_o6, _604ds_g1, _604ds_g3);
  and and_30 (d_S, _604ds_o6, _604ds_g5);
  and and_31 (_604es_o6, _604es_g1, _604es_g3);
  and and_32 (e_S, _604es_o6, _604es_g5);

  // Other names for the same wires on the sheet: _604ao_o15 = a_O; _604as_o8 = a_S; _604bo_o19 = b_O; _604bs_o9 = b_S;
  //   _604co_o19 = c_O; _604cs_o9 = c_S; _604do_o23 = d_O; _604ds_o7 = d_S; _604eo_o27 = e_O; _604es_o7 = e_S

  // Notes on the sheet:
  //   Guia_0604 - Maxtermos de 4 variaveis e simplificacao
  //   a) Pi M(2,6,7,14)
  //   Simplificada: (X+Z+W').(X+W'+Y').(Z+W'+Y')
  //   ORIGINAL / CANONICA
  //   b) Pi M(4,7,9,13,15)
  //   Simplificada: (W+X'+Z').(W+X+Z+Y').(W'+Y'+Z')
  //   ORIGINAL / CANONICA
  //   c) Pi M(4,6,8,14,15)
  //   Simplificada: (X+Z+Y').(W+Y+Z+X').(W'+X'+Y')
  //   ORIGINAL / CANONICA
  //   d) Pi M(1,5,7,12,13,15)
  //   Simplificada: (Y'+Z').(W+X+Z').(W+X'+Y')
  //   ORIGINAL / CANONICA
  //   e) Pi M(2,3,4,6,11,12,14)
  //   Simplificada: (Z+Y').(X+Y+W').(Y+W'+Z')
  //   ORIGINAL / CANONICA
  //   SIMPLIFICADA
  //   SIMPLIFICADA
  //   SIMPLIFICADA
  //   SIMPLIFICADA
  //   SIMPLIFICADA
endmodule

module Guia_0605 (
  input  x,
  input  y,
  input  z,
  output s_original,
  output s_simplificada
);

  wire _605_w1, _605_w2, _605_w3, _605_w4, _605_w5, _605_w6, _605_w7, _605_w10, _605simp_g1, _605simp_g2, nx,
       ny, nz;

  not not_1 (nx, x);
  not not_2 (ny, y);
  not not_3 (nz, z);
  and and_1 (_605simp_g1, x, ny);
  and and_2 (_605simp_g2, x, nz);
  or or_1 (_605_w5, ny, nx);
  and and_3 (_605_w6, x, y);
  and and_4 (_605_w10, y, z);
  not not_4 (_605_w3, _605_w5);
  not not_5 (_605_w4, _605_w6);
  or or_2 (_605_w7, _605_w10, nx);
  and and_5 (_605_w1, _605_w3, _605_w4);
  not not_6 (_605_w2, _605_w7);
  or or_3 (s_simplificada, _605simp_g1, _605simp_g2);
  or or_4 (s_original, _605_w1, _605_w2);

  // Other names for the same wires on the sheet: _605_sO = s_original; _605simp_o3 = s_simplificada

  // Notes on the sheet:
  //   Guia_0605 - Circuito fornecido e simplificacao por mintermos
  //   Circuito fornecido no enunciado
  //   Simplificada: s = x.y' + x.z' = x.(y' + z')
endmodule

module Guia_0606 (
  input  x,
  input  y,
  input  w,
  input  z,
  output s_original,
  output s_simplificada
);

  wire _606_w1, _606_w2, _606_w3, _606_w4, _606_w5_g1, _606_w5_g2, _606_w6_g1, _606_w6_g2, _606_w7,
       _606_w11_g1, _606_w11_g2, _606simp_g1, _606simp_g2, nw, nx, ny, nz;

  not not_1 (nx, x);
  not not_2 (ny, y);
  not not_3 (nw, w);
  not not_4 (nz, z);
  or or_1 (_606_w5_g1, ny, w);
  and and_1 (_606_w6_g1, x, y);
  and and_2 (_606_w11_g1, y, w);
  or or_2 (_606simp_g1, ny, nw);
  or or_3 (_606_w5_g2, _606_w5_g1, nx);
  and and_3 (_606_w6_g2, _606_w6_g1, nw);
  and and_4 (_606_w11_g2, _606_w11_g1, z);
  or or_4 (_606simp_g2, _606simp_g1, nz);
  not not_5 (_606_w3, _606_w5_g2);
  not not_6 (_606_w4, _606_w6_g2);
  or or_5 (_606_w7, _606_w11_g2, nx);
  not not_7 (_606_w2, _606_w7);
  and and_5 (s_simplificada, x, _606simp_g2);
  and and_6 (_606_w1, _606_w3, _606_w4);
  or or_6 (s_original, _606_w1, _606_w2);

  // Other names for the same wires on the sheet: _606_sO = s_original; _606_sS = s_simplificada

  // Notes on the sheet:
  //   Guia_0606 - Circuito fornecido e simplificacao por maxtermos
  //   Circuito fornecido no enunciado
  //   Simplificada: s = x.(y' + w' + z')
endmodule
